# Fritzing sketch arduino drone22 MegaUno Sketch (saved by Fritzing 0.9.3b)
circuit board: 13.6cm x 6.2cm
circuit board: 5.78556cm x 20cm
circuit board: 5.78556cm x 20cm
breadboards: 1

parts:
  GY801 = InvenSense MPU6050
  LED_Green = LED - 5mm [color="Green (565nm)" part_number="5mm green LED" package="5 mm [THT]"]
  LED_Yellow = LED - 5mm [color="Yellow (592nm)" part_number="5mm yellow LED" package="5 mm [THT]"]
  1K = Resistor [tolerance=±5% resistance=1k part_number=1k package=THT]
  -_+ = screw terminal, 2 pins
  50k = Resistor [tolerance=±5% resistance=50k part_number=50k package=THT]
  20k = Resistor [tolerance=±5% resistance=20k part_number=20k package=THT]
  30k = Resistor [tolerance=±5% resistance=30k part_number=30k package=THT]
  5V_Reg = Voltage Regulator - 5V [part_number="Reg 5V 7805CV" package="TO220 [THT]"]
  LED_Blue = LED - 5mm [color="Blue (525nm)" part_number="5mm blue LED" package="5 mm [THT]"]
  1K_2 = Resistor [tolerance=±5% resistance=1k part_number=1k package=THT]
  Synerduino_KWAD_Shield_V1_1 = Arduino Mega ADK (Rev3)
  ~ = male pin header, 12 pins [form="♂ (male)"]
  - = male pin header, 12 pins [form="♂ (male)"]
  + = male pin header, 12 pins [form="♂ (male)"]
  +_2 = male pin header, 8 pins [form="♂ (male)"]
  -_2 = male pin header, 8 pins [form="♂ (male)"]
  44 = male pin header, 3 pins [form="♂ (male)"]
  45 = male pin header, 3 pins [form="♂ (male)"]
  46 = male pin header, 3 pins [form="♂ (male)"]
  2_+_G_RxTx = male pin header, 4 pins [form="♂ (male)"]
  1_+_G_RxTx = male pin header, 4 pins [form="♂ (male)"]
  +_470uf_- = Electrolytic Capacitor [capacitance=470µF voltage=35V part_number=470µF package="200 mil [THT, electrolytic]"]
  ~_2 = male pin header, 8 pins [form="♂ (male)"]
  3_+_G_RxTx = male pin header, 4 pins [form="♂ (male)"]
  V+_TX_RX_Gn = male pin header, 4 pins [form="♂ (male)"]
  A0 = male pin header, 3 pins [form="♂ (male)"]
  -_+_~ = male pin header, 3 pins [form="♂ (male)"]
  -_+_2 = screw terminal, 2 pins
  0_-_+ = screw terminal, 2 pins
  3_-_+ = screw terminal, 2 pins
  -_+_1 = screw terminal, 2 pins
  REG_IN = Pad [width=2.2000000000000002 height=2 connect=center]
  5V_1A = Pad [width=2.2000000000000002 height=2 connect=center]
  D1 = Rectifier Diode [part_number=1N4001 package="300 mil [THT]"]
  3s = Pad [width=2.2000000000000002 height=2 connect=center]
  4s = Pad [width=2.2000000000000002 height=2 connect=center]
  VBAT = Pad [width=2.2000000000000002 height=2 connect=center]
  BEC = Pad [width=2.2000000000000002 height=2 connect=center]
  REG = Pad [width=2.2000000000000002 height=2 connect=center]
  / = Pad [width=2.2000000000000002 height=2 connect=center]
  V3 = Pad [width=2.2000000000000002 height=2 connect=center]
  V5 = Pad [width=2.2000000000000002 height=2 connect=center]
  /_2 = Pad [width=2.2000000000000002 height=2 connect=center]
  SENS = Pad [width=2.2000000000000002 height=2 connect=center]
  SELECTORS = Pad [width=2.2000000000000002 height=2 connect=center]
  A0_2 = Pad [width=2 height=2 connect=center]
  A1 = Pad [width=2 height=2 connect=center]
  A2 = Pad [width=2 height=2 connect=center]
  A3 = Pad [width=2 height=2 connect=center]
  SCL = Pad [width=2 height=2 connect=center]
  SDA = Pad [width=2 height=2 connect=center]
  +_G_RxTx = male pin header, 4 pins [form="♂ (male)"]
  1K_3 = Resistor [tolerance=±5% resistance=1k part_number=1k package=THT]

nets:
  VCC: GY801.VCC, Synerduino_KWAD_Shield_V1_1.3V3, V3.pad
  GND: GY801.GND, LED_Green.cathode, LED_Yellow.cathode, -_+.pin2, 5V_Reg.GND, LED_Blue.cathode, Synerduino_KWAD_Shield_V1_1.GND, -.pin1, -.pin2, -.pin3, -.pin4, -.pin5, -.pin6, -.pin7, -.pin8, -.pin9, -.pin10, -.pin11, -.pin12, -_2.pin1, -_2.pin2, -_2.pin3, -_2.pin4, -_2.pin5, -_2.pin6, -_2.pin7, -_2.pin8, 44.pin3, 45.pin3, 46.pin3, 2_+_G_RxTx.pin3, 1_+_G_RxTx.pin3, +_470uf_-.+, 3_+_G_RxTx.pin3, V+_TX_RX_Gn.pin1, A0.pin3, -_+_~.pin3, -_+_2.pin2, 0_-_+.pin2, 3_-_+.pin2, -_+_1.pin2, VBAT.pad, +_G_RxTx.pin3
  N1: GY801.SCL, Synerduino_KWAD_Shield_V1_1.A5, Synerduino_KWAD_Shield_V1_1.D21/SCL, SCL.pad
  N2: GY801.SDA, Synerduino_KWAD_Shield_V1_1.A4, Synerduino_KWAD_Shield_V1_1.D20/SDA, SDA.pad
  N3: LED_Green.anode, 1K.Pin_1
  N4: LED_Yellow.anode, 1K_3.Pin_1
  N5: 1K.Pin_0, Synerduino_KWAD_Shield_V1_1.D30
  N6: -_+.pin1, 50k.Pin_0, +_470uf_-.-, -_+_2.pin1, 0_-_+.pin1, 3_-_+.pin1, -_+_1.pin1, D1.anode
  N7: 50k.Pin_1, 20k.Pin_1, 30k.Pin_1, SENS.pad
  N8: 20k.Pin_0, 4s.pad
  N9: 30k.Pin_0, 3s.pad
  N10: 5V_Reg.input_voltage, REG_IN.pad
  N11: 5V_Reg.output_voltage, REG.pad
  N12: LED_Blue.anode, 1K_2.Pin_0
  N13: 1K_2.Pin_1, Synerduino_KWAD_Shield_V1_1.D13_PWM, ~.pin12
  N14: Synerduino_KWAD_Shield_V1_1.A8, ~_2.pin8
  N15: Synerduino_KWAD_Shield_V1_1.A9, ~_2.pin7
  N16: Synerduino_KWAD_Shield_V1_1.A10, ~_2.pin6
  N17: Synerduino_KWAD_Shield_V1_1.A11, ~_2.pin5
  N18: Synerduino_KWAD_Shield_V1_1.A12, ~_2.pin4
  N19: Synerduino_KWAD_Shield_V1_1.A13, ~_2.pin3
  N20: Synerduino_KWAD_Shield_V1_1.A14, ~_2.pin2
  N21: Synerduino_KWAD_Shield_V1_1.A15, ~_2.pin1
  N22: Synerduino_KWAD_Shield_V1_1.A0, A0.pin1, -_+_~.pin1, SELECTORS.pad, A0_2.pad
  N23: Synerduino_KWAD_Shield_V1_1.A1, A1.pad
  N24: Synerduino_KWAD_Shield_V1_1.A2, A2.pad
  N25: Synerduino_KWAD_Shield_V1_1.A3, A3.pad
  N26: Synerduino_KWAD_Shield_V1_1.D19/RX1, 1_+_G_RxTx.pin2
  N27: Synerduino_KWAD_Shield_V1_1.D18/TX1, 1_+_G_RxTx.pin1
  N28: Synerduino_KWAD_Shield_V1_1.D17/RX2, 2_+_G_RxTx.pin2, V+_TX_RX_Gn.pin2
  N29: Synerduino_KWAD_Shield_V1_1.D16/TX2, 2_+_G_RxTx.pin1, V+_TX_RX_Gn.pin3
  N30: Synerduino_KWAD_Shield_V1_1.D15/RX3, 3_+_G_RxTx.pin2
  N31: Synerduino_KWAD_Shield_V1_1.D14/TX3, 3_+_G_RxTx.pin1
  N32: Synerduino_KWAD_Shield_V1_1.D12_PWM, ~.pin11
  N33: Synerduino_KWAD_Shield_V1_1.D11_PWM, ~.pin10
  N34: Synerduino_KWAD_Shield_V1_1.D10_PWM, ~.pin9
  N35: Synerduino_KWAD_Shield_V1_1.D9_PWM, ~.pin8
  N36: Synerduino_KWAD_Shield_V1_1.D8_PWM, ~.pin7
  N37: Synerduino_KWAD_Shield_V1_1.5V, 2_+_G_RxTx.pin4, 1_+_G_RxTx.pin4, 3_+_G_RxTx.pin4, V5.pad, +_G_RxTx.pin4
  N38: Synerduino_KWAD_Shield_V1_1.VIN, /.pad
  N39: Synerduino_KWAD_Shield_V1_1.D0/RX0, +_G_RxTx.pin2
  N40: Synerduino_KWAD_Shield_V1_1.D1/TX0, +_G_RxTx.pin1
  N41: Synerduino_KWAD_Shield_V1_1.D2_PWM, ~.pin1
  N42: Synerduino_KWAD_Shield_V1_1.D3_PWM, ~.pin2
  N43: Synerduino_KWAD_Shield_V1_1.D4_PWM, ~.pin3
  N44: Synerduino_KWAD_Shield_V1_1.D5_PWM, ~.pin4
  N45: Synerduino_KWAD_Shield_V1_1.D6_PWM, ~.pin5
  N46: Synerduino_KWAD_Shield_V1_1.D7_PWM, ~.pin6
  N47: Synerduino_KWAD_Shield_V1_1.D31, 1K_3.Pin_0
  N48: Synerduino_KWAD_Shield_V1_1.D44, 44.pin1
  N49: Synerduino_KWAD_Shield_V1_1.D45, 45.pin1
  N50: Synerduino_KWAD_Shield_V1_1.D46, 46.pin1
  N51: +.pin1, +.pin2, +.pin3, +.pin4, +.pin5, +.pin6, +.pin7, +.pin8, +.pin9, +.pin10, +.pin11, +.pin12, +_2.pin1, +_2.pin2, +_2.pin3, +_2.pin4, +_2.pin5, +_2.pin6, +_2.pin7, +_2.pin8, 44.pin2, 45.pin2, 46.pin2, A0.pin2, -_+_~.pin2, BEC.pad
  N52: V+_TX_RX_Gn.pin4, /_2.pad
  N53: 5V_1A.pad, D1.cathode

notes:
  www.synerflight.com
  GPS
  Telemetey
  ~ + -
  3.3V
  VCC
  - + ~
