# Fritzing sketch arduino drone24-1 MegaUno Sketch (Printed 2021) (saved by Fritzing 0.9.3b)
circuit board: 5.78556cm x 20cm
circuit board: 13.6cm x 6.2cm
circuit board: 5.78556cm x 20cm
breadboards: 1

parts:
  GY801 = InvenSense MPU6050
  D3-Green = LED - 5mm [color="Green (565nm)" part_number="5mm green LED" package="5 mm [THT]"]
  D4-Yellow = LED - 5mm [color="Yellow (592nm)" part_number="5mm yellow LED" package="5 mm [THT]"]
  R3 = Resistor [tolerance=±5% resistance=1k part_number=1k package=THT]
  -_+ = screw terminal, 2 pins
  R4 = Resistor [tolerance=±5% resistance=51k part_number=50k package=THT]
  R5 = Resistor [tolerance=±5% resistance=20k part_number=20k package=THT]
  R6 = Resistor [tolerance=±5% resistance=30k part_number=30k package=THT]
  U1 = Voltage Regulator - 5V [part_number="REG1 5V 7805CV" package="TO220 [THT]"]
  D2-Blue = LED - 5mm [color="Blue (525nm)" part_number="5mm blue LED" package="5 mm [THT]"]
  R1 = Resistor [tolerance=±5% resistance=1k part_number=1k package=THT]
  Synerduino_KWAD_Shield_V1_1 = Arduino Mega ADK (Rev3)
  J6 = male pin header, 12 pins [form="♂ (male)"]
  J8 = male pin header, 12 pins [form="♂ (male)"]
  J7 = male pin header, 12 pins [form="♂ (male)"]
  J10 = male pin header, 8 pins [form="♂ (male)"]
  J9 = male pin header, 8 pins [form="♂ (male)"]
  J23 = male pin header, 3 pins [form="♂ (male)"]
  J22 = male pin header, 3 pins [form="♂ (male)"]
  J21 = male pin header, 3 pins [form="♂ (male)"]
  J3 = male pin header, 4 pins [form="♂ (male)"]
  J4 = male pin header, 4 pins [form="♂ (male)"]
  C1 = Electrolytic Capacitor [capacitance=470µF voltage=35V part_number=470µF package="200 mil [THT, electrolytic]"]
  J11 = male pin header, 8 pins [form="♂ (male)"]
  J2 = male pin header, 4 pins [form="♂ (male)"]
  J5 = male pin header, 4 pins [form="♂ (male)"]
  J20 = male pin header, 3 pins [form="♂ (male)"]
  -_+_2 = screw terminal, 2 pins
  0_-_+ = screw terminal, 2 pins
  3_-_+ = screw terminal, 2 pins
  -_+_1 = screw terminal, 2 pins
  D1 = Rectifier Diode [part_number=1N4001 package="300 mil [THT]"]
  P3 = Pad [width=2.2000000000000002 height=2 connect=center]
  P1 = Pad [width=2.2000000000000002 height=2 connect=center]
  P2 = Pad [width=2.2000000000000002 height=2 connect=center]
  P5 = Pad [width=2.2000000000000002 height=2 connect=center]
  P4 = Pad [width=2.2000000000000002 height=2 connect=center]
  P6 = Pad [width=2.2000000000000002 height=2 connect=center]
  P8 = Pad [width=2.2000000000000002 height=2 connect=center]
  P7 = Pad [width=2.2000000000000002 height=2 connect=center]
  P9 = Pad [width=2.2000000000000002 height=2 connect=center]
  P10 = Pad [width=2.2000000000000002 height=2 connect=center]
  A0 = Pad [width=2 height=2 connect=center]
  A1 = Pad [width=2 height=2 connect=center]
  A2 = Pad [width=2 height=2 connect=center]
  A3 = Pad [width=2 height=2 connect=center]
  SCL = Pad [width=2 height=2 connect=center]
  SDA = Pad [width=2 height=2 connect=center]
  J1 = male pin header, 4 pins [form="♂ (male)"]
  R2 = Resistor [tolerance=±5% resistance=1k part_number=1k package=THT]
  J17 = male pin header, 10 pins [form="♂ (male)"]  # not connected
  J18 = double row male pin header, 36 pins [form="♂ (male)"]  # not connected
  J12 = male pin header, 8 pins [form="♂ (male)"]  # not connected
  J13 = male pin header, 8 pins [form="♂ (male)"]  # not connected
  J15 = male pin header, 8 pins [form="♂ (male)"]  # not connected
  J16 = male pin header, 8 pins [form="♂ (male)"]  # not connected
  J14 = male pin header, 8 pins [form="♂ (male)"]  # not connected
  J19 = male pin header, 3 pins [form="♂ (male)"]

nets:
  VCC: GY801.VCC, Synerduino_KWAD_Shield_V1_1.3V3, P6.pad
  GND: GY801.GND, D3-Green.cathode, D4-Yellow.cathode, -_+.pin2, U1.GND, D2-Blue.cathode, Synerduino_KWAD_Shield_V1_1.GND, J8.pin1, J8.pin2, J8.pin3, J8.pin4, J8.pin5, J8.pin6, J8.pin7, J8.pin8, J8.pin9, J8.pin10, J8.pin11, J8.pin12, J9.pin1, J9.pin2, J9.pin3, J9.pin4, J9.pin5, J9.pin6, J9.pin7, J9.pin8, J23.pin3, J22.pin3, J21.pin3, J3.pin3, J4.pin3, C1.+, J2.pin3, J5.pin1, J20.pin3, -_+_2.pin2, 0_-_+.pin2, 3_-_+.pin2, -_+_1.pin2, P2.pad, J1.pin3, J19.pin3
  N1: GY801.SCL, Synerduino_KWAD_Shield_V1_1.A5, Synerduino_KWAD_Shield_V1_1.D21/SCL, SCL.pad
  N2: GY801.SDA, Synerduino_KWAD_Shield_V1_1.A4, Synerduino_KWAD_Shield_V1_1.D20/SDA, SDA.pad
  N3: D3-Green.anode, R3.Pin_1
  N4: D4-Yellow.anode, R2.Pin_1
  N5: R3.Pin_0, Synerduino_KWAD_Shield_V1_1.D30
  N6: -_+.pin1, R4.Pin_0, C1.-, -_+_2.pin1, 0_-_+.pin1, 3_-_+.pin1, -_+_1.pin1, D1.anode
  N7: R4.Pin_1, R5.Pin_1, R6.Pin_1, P9.pad
  N8: R5.Pin_0, P1.pad
  N9: R6.Pin_0, P3.pad
  N10: U1.input_voltage, D1.cathode
  N11: U1.output_voltage, Synerduino_KWAD_Shield_V1_1.VIN, P4.pad
  N12: D2-Blue.anode, R1.Pin_0
  N13: R1.Pin_1, Synerduino_KWAD_Shield_V1_1.D13_PWM, J6.pin12
  N14: Synerduino_KWAD_Shield_V1_1.A8, J11.pin8
  N15: Synerduino_KWAD_Shield_V1_1.A9, J11.pin7
  N16: Synerduino_KWAD_Shield_V1_1.A10, J11.pin6
  N17: Synerduino_KWAD_Shield_V1_1.A11, J11.pin5
  N18: Synerduino_KWAD_Shield_V1_1.A12, J11.pin4
  N19: Synerduino_KWAD_Shield_V1_1.A13, J11.pin3
  N20: Synerduino_KWAD_Shield_V1_1.A14, J11.pin2
  N21: Synerduino_KWAD_Shield_V1_1.A15, J11.pin1
  N22: Synerduino_KWAD_Shield_V1_1.A0, J20.pin1, P10.pad, A0.pad, J19.pin1
  N23: Synerduino_KWAD_Shield_V1_1.A1, A1.pad
  N24: Synerduino_KWAD_Shield_V1_1.A2, A2.pad
  N25: Synerduino_KWAD_Shield_V1_1.A3, A3.pad
  N26: Synerduino_KWAD_Shield_V1_1.D19/RX1, J4.pin2
  N27: Synerduino_KWAD_Shield_V1_1.D18/TX1, J4.pin1
  N28: Synerduino_KWAD_Shield_V1_1.D17/RX2, J3.pin2, J5.pin2
  N29: Synerduino_KWAD_Shield_V1_1.D16/TX2, J3.pin1, J5.pin3
  N30: Synerduino_KWAD_Shield_V1_1.D15/RX3, J2.pin2
  N31: Synerduino_KWAD_Shield_V1_1.D14/TX3, J2.pin1
  N32: Synerduino_KWAD_Shield_V1_1.D12_PWM, J6.pin11
  N33: Synerduino_KWAD_Shield_V1_1.D11_PWM, J6.pin10
  N34: Synerduino_KWAD_Shield_V1_1.D10_PWM, J6.pin9
  N35: Synerduino_KWAD_Shield_V1_1.D9_PWM, J6.pin8
  N36: Synerduino_KWAD_Shield_V1_1.D8_PWM, J6.pin7
  N37: Synerduino_KWAD_Shield_V1_1.5V, J3.pin4, J4.pin4, J2.pin4, P8.pad, J1.pin4
  N38: Synerduino_KWAD_Shield_V1_1.D0/RX0, J1.pin2
  N39: Synerduino_KWAD_Shield_V1_1.D1/TX0, J1.pin1
  N40: Synerduino_KWAD_Shield_V1_1.D2_PWM, J6.pin1
  N41: Synerduino_KWAD_Shield_V1_1.D3_PWM, J6.pin2
  N42: Synerduino_KWAD_Shield_V1_1.D4_PWM, J6.pin3
  N43: Synerduino_KWAD_Shield_V1_1.D5_PWM, J6.pin4
  N44: Synerduino_KWAD_Shield_V1_1.D6_PWM, J6.pin5
  N45: Synerduino_KWAD_Shield_V1_1.D7_PWM, J6.pin6
  N46: Synerduino_KWAD_Shield_V1_1.D31, R2.Pin_0
  N47: Synerduino_KWAD_Shield_V1_1.D44, J23.pin1
  N48: Synerduino_KWAD_Shield_V1_1.D45, J22.pin1
  N49: Synerduino_KWAD_Shield_V1_1.D46, J21.pin1
  N50: J7.pin1, J7.pin2, J7.pin3, J7.pin4, J7.pin5, J7.pin6, J7.pin7, J7.pin8, J7.pin9, J7.pin10, J7.pin11, J7.pin12, J10.pin1, J10.pin2, J10.pin3, J10.pin4, J10.pin5, J10.pin6, J10.pin7, J10.pin8, J23.pin2, J22.pin2, J21.pin2, J20.pin2, P5.pad, J19.pin2
  N51: J5.pin4, P7.pad

notes:
  www.synerflight.com
  GPS
  2 + - Rx Tx
  1 + - Rx Tx
  3 + - Rx Tx
  ~ + -
  Telemetey
  3.3V
  VCC
  - + ~
  V3 GPS V5
  470uf
  1K
  1k
  51K
  20k
  30K
  +
  7805 CV
  1N4001
  0 + - Rx Tx
  2 + Tx Rx -
  4S  3S
  REG in
  AUX in
  SELECTORS
  TELE
  A0
  46
  45
  44
